# Fritzing sketch Test1 (saved by Fritzing 0.9.6b)
stripboards: 1

parts:
  U1 = Optocoupler [package=THT]
  LED1 = LED - 5mm [color="Red (633nm)" current=0.030 package="5 mm [THT]"]
  R1 = Resistor [tolerance=±5% power=0.25 resistance=1.5k package=THT]
  D1 = Rectifier Diode [part_number=1N4001 package="300 mil [THT]"]
  D2 = Rectifier Diode [part_number=1N4001 package="300 mil [THT]"]
  R3 = Resistor [tolerance=±5% power=0.25 resistance=1.8k package=THT]
  J1 = male pin header, 1 pin [form="♂ (male)"]
  J2 = male pin header, 1 pin [form="♂ (male)"]
  J3 = male pin header, 1 pin [form="♂ (male)"]
  J4 = male pin header, 1 pin [form="♂ (male)"]
  R4 = Resistor [tolerance=±5% power=0.25 resistance=2.0k package=THT]
  J5 = male pin header, 1 pin [form="♂ (male)"]
  J7 = male pin header, 1 pin [form="♂ (male)"]
  R5 = Resistor [tolerance=±5% power=0.25 resistance=10 package=THT]
  R6 = Resistor [tolerance=±5% power=0.25 resistance=1.5k package=THT]
  Q1 = PNP-Transistor [package="TO92 [THT]"]
  R7 = Resistor [tolerance=±5% power=0.25 resistance=10 package=THT]
  C2 = Ceramic Capacitor [capacitance=0.47µF voltage=35V package="100 mil [THT, multilayer]"]
  J8 = male pin header, 2 pins [form="♂ (male)"]
  J9 = male pin header, 3 pins [form="♂ (male)"]
  LED2 = LED - 5mm [color="Red (633nm)" current=0.030 package="5 mm [THT]"]
  J10 = male pin header, 1 pin [form="♂ (male)"]

nets:
  N1: U1.Pin_1, LED1.cathode
  N2: U1.Pin_2, J7.pin1, C2.1, J9.pin2
  N3: U1.Pin_4, J3.pin1, J8.pin2
  N4: U1.Pin_5, R3.Pin_0, J2.pin1
  N5: LED1.anode, R6.Pin_1
  N6: R1.Pin_0, J1.pin1, Q1.C, C2.0
  N7: R1.Pin_1, R6.Pin_0
  N8: D1.cathode, D2.anode, R4.Pin_1, R7.Pin_1
  N9: D1.anode, D2.cathode, J4.pin1, Q1.E, J9.pin1
  N10: R3.Pin_1, LED2.cathode
  N11: R4.Pin_0, J5.pin1, J9.pin3
  N12: R5.Pin_0, R7.Pin_0
  N13: R5.Pin_1, Q1.B
  N14: J8.pin1, LED2.anode, J10.pin1
